# Fritzing sketch RGB_LED_Mixer (saved by Fritzing 0.9.3b)
breadboards: 1

parts:
  Part1 = Arduino Uno (Rev3)
  LED1 = RGB LED - (4 legs) [package="5 mm [THT]"]
  R1 = Resistor [tolerance=±5% resistance=330 package=THT]
  R2 = Resistor [tolerance=±5% resistance=330 package=THT]
  R3 = Resistor [tolerance=±5% resistance=330 package=THT]
  R4 = Rotary Potentiometer (Small) [maximum_resistance=100kΩ package=THT]
  R5 = Rotary Potentiometer (Small) [maximum_resistance=100kΩ package=THT]
  R6 = Rotary Potentiometer (Small) [maximum_resistance=100kΩ package=THT]

nets:
  N1: Part1.A0, R4.wiper
  N2: Part1.A1, R5.wiper
  N3: Part1.A2, R6.wiper
  N4: Part1.D8, R3.Pin_0
  N5: Part1.D9_PWM, R2.Pin_0
  N6: Part1.D10_PWM/SS, R1.Pin_0
  N7: Part1.5V, LED1.common_anode, R4.leg2, R5.leg2, R6.leg2
  N8: Part1.GND, R4.leg1, R5.leg1, R6.leg1
  N9: LED1.red_cathode, R1.Pin_1
  N10: LED1.green_cathode, R2.Pin_1
  N11: LED1.blue_cathode, R3.Pin_1
